# Fritzing sketch emitter (saved by Fritzing 0.9.4)
breadboards: 1

parts:
  Xenon1 = Particle Xenon
  Micro_switch = SPST Switch [package=switch-spdt_lock.007s]
  Lipo = LIPO-1000mAh [package=lipo-1000]
  JP1 = Header 2 [package=jst-2-smd]

nets:
  N1: Xenon1.3.3V, Micro_switch.P
  N2: Xenon1.D8, Micro_switch.S
  N3: Lipo.+, JP1.2
  N4: Lipo.-, JP1.1

custom parts:
  Particle Xenon: The Boron LTE is a powerful LTE CAT-M1 enabled development kit that can act as either a standalone cellular device or LTE enabled gateway, repeater, or endpoint for a Particle Mesh networks. Equipped with the Nordic nRF52840 and u-blox SARA 410 processors, the Boron has built-in battery charging circuitry which makes it easier to connect a Li-Po battery and 20 mixed signal GPIOs to interface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
