# Fritzing sketch receiver (saved by Fritzing 0.9.4)
breadboards: 1

parts:
  Xenon1 = Particle Xenon
  DFRobot_DFPlayer_Mini1 = DFRobot DFPlayer Mini [part_number=DFR0299]
  RGB_LED = RGB LED - (4 legs) [package="5 mm [THT]"]
  R1 = Resistor [tolerance=±5% resistance=330 package="1206 [SMD]"]
  R2 = Resistor [tolerance=±5% resistance=330 package="1206 [SMD]"]
  R3 = Resistor [tolerance=±5% resistance=330 package="1206 [SMD]"]
  SP1 = SPEAKER [package=pcb_mount_speaker]

nets:
  N1: Xenon1.GND, DFRobot_DFPlayer_Mini1.GND-1, DFRobot_DFPlayer_Mini1.GND-2, RGB_LED.common_anode
  N2: Xenon1.RX, DFRobot_DFPlayer_Mini1.TX
  N3: Xenon1.TX, DFRobot_DFPlayer_Mini1.RX
  N4: Xenon1.D2, R1.Pin_0
  N5: Xenon1.D3, R2.Pin_0
  N6: Xenon1.D4, R3.Pin_0
  N7: Xenon1.VUSB, DFRobot_DFPlayer_Mini1.VCC
  N8: DFRobot_DFPlayer_Mini1.SPK_1, SP1.+
  N9: DFRobot_DFPlayer_Mini1.SPK_2, SP1.-
  N10: RGB_LED.red_cathode, R1.Pin_1
  N11: RGB_LED.green_cathode, R2.Pin_1
  N12: RGB_LED.blue_cathode, R3.Pin_1

custom parts:
  Particle Xenon: The Boron LTE is a powerful LTE CAT-M1 enabled development kit that can act as either a standalone cellular device or LTE enabled gateway, repeater, or endpoint for a Particle Mesh networks. Equipped with the Nordic nRF52840 and u-blox SARA 410 processors, the Boron has built-in battery charging circuitry which makes it easier to connect a Li-Po battery and 20 mixed signal GPIOs to interface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
